# Fritzing sketch Connections (saved by Fritzing 0.9.3b)
breadboards: 1

parts:
  Part1 = Arduino Mega ADK (Rev3)
  Part1_2 = Arduino Mega ADK (Rev3)
  Part1_3 = Arduino Mega 2560 (Rev3)
  J1 = Piezo Speaker

nets:
  N1: Part1.A7, J1.pin2
  GND: Part1.GND, Part1_2.GND, Part1_3.GND, J1.pin1
  5V: Part1.5V, Part1_2.5V, Part1_3.5V
